// Logisim project anikanawer2107089.circ as structural Verilog
module sevensegmentbcd (
  input  A,
  input  B,
  input  D,
  input  C,
  output a_2,
  output b_2,
  output c_2,
  output d_2,
  output e,
  output f,
  output g
);

  wire and_1_out, and_2_out, and_3_out, and_4_out, and_5_out, and_6_out, and_7_out, and_8_out, and_9_out,
       not_1_out, not_2_out, not_3_out, or_1_out, or_2_out, or_4_out, or_5_out, or_6_out, or_7_out, or_8_out,
       or_10_out, or_14_out;

  not not_1 (not_1_out, C);
  not not_2 (not_2_out, B);
  not not_3 (not_3_out, D);
  and and_1 (and_1_out, B, D);
  and and_2 (and_2_out, and_1_out, not_1_out);
  and and_3 (and_3_out, B, not_1_out);
  and and_4 (and_4_out, C, not_2_out);
  and and_5 (and_5_out, not_1_out, not_3_out);
  and and_6 (and_6_out, not_2_out, not_3_out);
  and and_7 (and_7_out, C, not_3_out);
  and and_8 (and_8_out, B, not_3_out);
  and and_9 (and_9_out, C, D);
  or or_1 (or_1_out, A, C);
  or or_2 (or_2_out, A, not_2_out);
  or or_3 (e, and_6_out, and_7_out);
  or or_4 (or_4_out, A, and_3_out);
  or or_5 (or_5_out, and_6_out, and_1_out);
  or or_6 (or_6_out, and_5_out, and_9_out);
  or or_7 (or_7_out, B, not_1_out);
  or or_8 (or_8_out, A, and_4_out);
  or or_9 (b_2, or_2_out, or_6_out);
  or or_10 (or_10_out, or_4_out, and_8_out);
  or or_11 (g, or_10_out, and_4_out);
  or or_12 (a_2, or_1_out, or_5_out);
  or or_13 (c_2, or_7_out, D);
  or or_14 (or_14_out, or_8_out, e);
  or or_15 (d_2, or_14_out, and_2_out);
  or or_16 (f, or_10_out, and_5_out);
  _7_Segment_Display u_7_segment_display_1 (.g(g), .f(f), .a(a_2), .b(b_2), .e(e), .d(d_2), .c(c_2));  // open: dp

  // Notes on the sheet:
  //   2107089
endmodule

module minuteseco (
  input  Clock_Pluse,
  output si0,
  output clk_out,
  output si1,
  output si2,
  output si3,
  output Sl0,
  output sl1,
  output ml2,
  output ml1,
  output ml0,
  output mi3,
  output mi2,
  output mi1,
  output mi0,
  output sl2
);

  wire nand_1_out, not_1_out, not_2_out, not_3_out;

  nand nand_1 (nand_1_out, sl2, not_3_out, Sl0, si3, not_2_out, not_1_out, si0);
  // Circuitmostimportant circuitmostimportant_1: pin names not known; wires that end beside it: sl2, sl1, Sl0, Clock_Pluse, si3, si2, si1, si0
  not not_1 (not_1_out, si1);
  not not_2 (not_2_out, si2);
  not not_3 (not_3_out, sl1);
  // Circuitmostimportant circuitmostimportant_2: pin names not known; wires that end beside it: ml2, ml1, ml0, nand_1_out, mi3, mi2, mi1, mi0, clk_out

  // Notes on the sheet:
  //   2107089
endmodule
